# Fritzing sketch layout (saved by Fritzing 0.9.4)

parts:
  RHT1 = Humidity and Temperature Sensor RHT03
  VCC1 = Battery
  WeMos_D1_Mini1 = WeMos D1 Mini

nets:
  VCC: RHT1.Vcc, VCC1.+, WeMos_D1_Mini1.3V3
  N1: RHT1.Data-signal, WeMos_D1_Mini1.D4
  N2: RHT1.GND_2, VCC1.-, WeMos_D1_Mini1.G
